# Fritzing sketch Joystick (saved by Fritzing 0.9.6b)

parts:
  Part2 = Black Joystick KY-023
  BAT2 = Battery Holders [package=lipo-1100mAh]
  M1 = DOIT Esp32 DevKit v1 (30 pins long, 11 pins width) [part_number=ESP32S-PIN30]
  R1 = Resistor [tolerance=±5% resistance=1k package="2512 [SMD]"]
  S3 = Pushbutton [package="[THT]"]
  TP2 = TP4056 [chip_label=TP4056 package="DIP (Dual Inline) [THT]"]
  S4 = Toggle Switch [package=THT]
  LED2 = RGB LED - (4 legs) [package="5 mm [THT]"]
  R2 = Resistor [tolerance=±5% resistance=220 package="0402 [SMD]"]

nets (from the breadboard view):
  N1: Part2.SW, M1.TX2
  N2: Part2.VRy, M1.VP
  N3: Part2.VRx, M1.VN
  +5V: Part2.+5V, M1.3V3, S4.L2, R2.Pin_0
  GND: Part2.GND, M1.GND, R1.Pin_1, TP2.pin6, S4.L1
  N4: BAT2.+, TP2.pin4
  N5: BAT2.-, TP2.pin5
  N6: M1.D4, R1.Pin_0, S3.Pin_3, S3.Pin_4
  N7: M1.D21, LED2.red_cathode
  N8: M1.D22, LED2.blue_cathode
  N9: M1.D23, LED2.green_cathode
  N10: S3.Pin_1, S3.Pin_2, TP2.pin3, S4.COM

custom parts:
  Black Joystick KY-023: Description: The joystick is a combination of 2 analoog potentiometer and a digital switch. Arduino GND --> Module pin - Arduino +5V --> Module pin +5V Arduino Analoog 0 --> Module VRx Arduino Analoog 1 --> Module VRy Arduino Digital --> Module SW Dimensions: 1" x 1.25"
  DOIT Esp32 DevKit v1 (30 pins long, 11 pins width): The DOIT Esp32 DevKit v1 is one of the development board created by DOIT to evaluate the ESP-WROOM-32 module. It is based on the ESP32 microcontroller that boasts Wifi, Bluetooth, Ethernet and Low Power support all in a single chip. (vanepp) made breadboard work, adjusted pin numbering and labels and reduced size of schematic and cleaned up pcb. This chip is 30pins long (2 x15) and 11 pins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
  TP4056: A DIP stand-in part for whatever IC you want. With 6 pins on a 300mil dual inline package (DIP) footprint.
